# Fritzing sketch Schematic_air_monitoring (saved by Fritzing 0.9.3b)
circuit board: 8.46667cm x 5.64444cm
breadboards: 1

parts:
  Part1 = Arduino Uno (Rev3)
  R1 = Trimmer Potentiometer [maximum_resistance=10kΩ package=THT]
  DHT1 = Humidity and Temperature Sensor DHT11
  U1 = LCD-16X2 [package=lcd-16x2_noholes]
  Part2 = Adafruit CCS811
  Part3 = MQ-3 breakout
  U2 = 4-Channel 5v Relay Shield [package=relay-4ch5v10a]

nets:
  N1: Part1.A0, Part3.AO
  N2: Part1.A4/SDA, Part2.SDA
  N3: Part1.A5/SCL, Part2.SCL
  N4: Part1.D8, U1.RS
  N5: Part1.D9_PWM, U1.E
  N6: Part1.D10_PWM/SS, DHT1.Data-signal
  GND: Part1.GND, DHT1.GND_2, U1.K, Part2.GND, Part2.!WAKE, Part3.GND, U2.GND
  N7: Part1.D0/RX, U2.IN1
  N8: Part1.D1/TX, U2.IN2
  N9: Part1.D2, U2.IN3
  N10: Part1.D3_PWM, U2.IN4
  N11: Part1.D4, U1.DB4
  N12: Part1.D5_PWM, U1.DB5
  N13: Part1.D6_PWM, U1.DB6
  N14: Part1.D7, U1.DB7
  VCC: Part1.5V, R1.leg1, DHT1.Vcc, Part2.VIN, Part3.VCC, U2.VCC
  N15: R1.leg2, U1.VO

custom parts:
  Humidity and Temperature Sensor DHT11: Digital relative humidity & temperature sensor DHT11
  MQ-3 breakout: Alcohol sensor is capable of detecting alcohol (ethanol) particles on itself and gives the information in digital form back to us to manipulate with it. SKU:101251 • Voltage: 5V DC • Power: max 750mW • Measurement range: 0.04-4mg/L
  4-Channel 5v Relay Shield: 4 Channel 5v Relay Shield w. 2x SPD-06VDC-SD-C

// code stored in the sketch: Code.ino
#include <dht.h>
#include <LiquidCrystal.h>
LiquidCrystal lcd(8,9,4,5,6,7);
#include <Adafruit_CCS811.h>

dht DHT;
#define DHT11_PIN 10
int eCO2;
int TVOC;

Adafruit_CCS811 ccs;

void setup() {
  Serial.begin(9600);
  pinMode(2,1);
  Serial.println("CCS811 test");
  lcd.begin(16,2);
  lcd.clear();
  if(!ccs.begin()){
    Serial.println("Failed to start sensor! Please check your wiring.");
    while(1);
  }
}

void loop() {
  if(ccs.available()){
    if(!ccs.readData()){
      eCO2 = ccs.geteCO2();
      TVOC = ccs.getTVOC();
      Serial.print("CO2: ");
      Serial.print(ccs.geteCO2());
      lcd.setCursor(0,0);
      lcd.print("CO2:");
      lcd.setCursor(4,0);
      lcd.print(eCO2);
      lcd.setCursor(9,0);
      lcd.print("TVOC:");
      lcd.setCursor(14,0);
      lcd.print(TVOC);
      Serial.print("ppm, TVOC: ");
      Serial.print(ccs.getTVOC());
      Serial.print("ppb");
    }
    else{
      Serial.println("ERROR!");
      while(1);
    }
  }
  
  int chk = DHT.read11(DHT11_PIN);
  int humidity= DHT.humidity;
  int temp_2 = DHT.temperature;
  int gas_data = analogRead(A0);
  lcd.setCursor(0,1);
  lcd.print("T:");
  lcd.setCursor(2,1);
  lcd.print(temp_2);
  lcd.setCursor(5,1);
  lcd.print("Hd:");
  lcd.setCursor(8,1);
  lcd.print(humidity);
  lcd.setCursor(11,1);
  lcd.print("O3:");
  lcd.setCursor(14,1);
  lcd.print(gas_data);
  Serial.print('\t');
  Serial.print(humidity);
  Serial.print('\t');
  Serial.print(temp_2);
  Serial.print('\t');
  Serial.println(gas_data);
  delay(2000);
  
     if(eCO2 >= 1000)
        {
          digitalWrite(2,1);
        }
           else
             {
               digitalWrite(2,0);
              }
}
